# Fritzing sketch led_motion_schematic (saved by Fritzing 0.9.3b)
breadboards: 1

parts:
  Part1 = Arduino Uno (Rev3)
  R1 = Resistor [tolerance=±5% resistance=220 package=THT]
  LED1 = LED - 5mm [color="Red (633nm)" package="5 mm [THT]"]
  LED2 = LED - 5mm [color="Red (633nm)" package="5 mm [THT]"]
  LED3 = LED - 5mm [color="Red (633nm)" package="5 mm [THT]"]
  LED4 = LED - 5mm [color="Red (633nm)" package="5 mm [THT]"]
  LED5 = LED - 5mm [color="Red (633nm)" package="5 mm [THT]"]
  LED6 = LED - 5mm [color="Red (633nm)" package="5 mm [THT]"]
  R2 = Resistor [tolerance=±5% resistance=220 package=THT]
  R3 = Resistor [tolerance=±5% resistance=220 package=THT]
  R4 = Resistor [tolerance=±5% resistance=220 package=THT]
  R5 = Resistor [tolerance=±5% resistance=220 package=THT]
  R6 = Resistor [tolerance=±5% resistance=220 package=THT]
  S1 = Pushbutton [package="[THT]"]
  R7 = Resistor [tolerance=±5% resistance=10k package=THT]
  PIR1 = PIR sensor
  S2 = Pushbutton [package="[THT]"]
  R10 = Resistor [tolerance=±5% resistance=10k package=THT]
  R11 = Rotary Potentiometer (Small) [maximum_resistance=100kΩ package=THT]
  R12 = Rotary Potentiometer (Small) [maximum_resistance=100kΩ package=THT]

nets:
  N1: Part1.A0, R11.wiper
  N2: Part1.A1, R12.wiper
  N3: Part1.D9_PWM, R4.Pin_0
  N4: Part1.D10_PWM/SS, R5.Pin_0
  N5: Part1.D11_PWM/MOSI, R6.Pin_0
  N6: Part1.D12/MISO, PIR1.SIG
  N7: Part1.D2, S1.Pin_1, S1.Pin_2, R7.Pin_0
  N8: Part1.D3_PWM, R1.Pin_0
  5V: Part1.D4, Part1.5V, S1.Pin_3, S1.Pin_4, PIR1.VDD, S2.Pin_3, S2.Pin_4, R11.leg2, R12.leg2
  N9: Part1.D5_PWM, R2.Pin_0
  N10: Part1.D6_PWM, R3.Pin_0
  GND: Part1.GND, LED1.cathode, LED2.cathode, LED3.cathode, LED4.cathode, LED5.cathode, LED6.cathode, R7.Pin_1, PIR1.GND, R10.Pin_1, R11.leg1, R12.leg1
  N11: R1.Pin_1, LED1.anode
  N12: LED2.anode, R2.Pin_1
  N13: LED3.anode, R3.Pin_1
  N14: LED4.anode, R4.Pin_1
  N15: LED5.anode, R5.Pin_1
  N16: LED6.anode, R6.Pin_1
  N17: S2.Pin_1, S2.Pin_2, R10.Pin_0

// code stored in the sketch: ledmotion.ino
/* 
   Motion detection using PIR motion sensor. Motion indicated by LEDs
   Same similar setup to led_wave
   Motion detector lights up LEDs when motion is detected
*/
// ******************************************
// Global variables Declaration - Mapping physical sensors connections to Arduino PINs
const int testButton=2;      
const int waveButton=4;      
const int speedControlPin = A0; 
const int brightnessControlPin = A1;
const int pirSensor=12;


// Mapping all LEDs physical connections to Arduino PINs
const int ledsPin[]={3,5,6,9,10,11};
boolean ledsOn=false;         // the present state of the LEDs (ON/OFF)  
boolean lastButton=LOW;       // the last button state
boolean currentButton=LOW;    // the current button state 
int pirState = LOW;           // used for the PIR sensor, assuming no motion detected
// ******************************************
void setup()
{
    pinMode (testButton, INPUT); // set test button as input 
    pinMode (waveButton, INPUT); // set wave animation button as input 
    for (int i=0; i<6; i++)        // set all LEDs to output 
      pinMode(ledsPin[i], OUTPUT);  
    // initialize serial communication at 9600 bits per second:
    Serial.begin(9600);
    // letting the PIR sensor to learn the environment 
    Serial.println("Initialization:"); 
    for(int i=0; i<10; i++){
      Serial.print("."); 
      delay(1000);
    } 
    Serial.println(""); 
    Serial.println("System is Ready"); 
}
// ******************************************
void loop()
{
  checkTestButton();
  checWaveButton();
  checkPIR();
}
// ******************************************
// if the button was pressed than wait for the button state to stablize and 
boolean debounce(int buttonPIN,boolean last)
{
  boolean current= digitalRead(buttonPIN);
  if (current != last) {
    delay(5); // wait 5ms for button state stablizing 
    current = digitalRead(buttonPIN); // read it again
  }
  return current; 
}
// ******************************************
// checking if the test button was pressed and turn ON or OFF all LEDs
void checkTestButton()
{
  currentButton = debounce(testButton,lastButton);  
  if (currentButton == HIGH && lastButton == LOW) // button was pressed 
     ledsOn =!ledsOn; //toggle the LEDs state
   lastButton = currentButton;
   for (int i=0; i<6; i++)
       digitalWrite(ledsPin[i], ledsOn);
}
// ******************************************
// checking if the wave button was pressed and run animation wave on LEDs 
void checWaveButton()
{
  int brightnessLevel=analogRead(brightnessControlPin); 
  int speedLevel=analogRead(speedControlPin);
// mapping the relevant ranges from the sensors reading 
  speedLevel=map(speedLevel, 0, 1023, 700, 100);
  brightnessLevel=map(brightnessLevel, 0, 1023, 0, 255);


  if(digitalRead(waveButton) == HIGH)// button is pressed 
  {
    Serial.println("Running Animation Wave with the following Parameters:"); 
    Serial.print("Speed:");
    Serial.println(speedLevel);
    Serial.print("Brightness:");
    Serial.println(brightnessLevel);
    for(int i=0; i<6; i++)
    {
//     digitalWrite(ledsPin[i], HIGH);
     analogWrite(ledsPin[i],brightnessLevel);
     delay(speedLevel);
     digitalWrite(ledsPin[i], LOW);
    }
    for(int i=5; i>=0; i--)
    {
//     digitalWrite(ledsPin[i], HIGH);
     analogWrite(ledsPin[i],brightnessLevel);
     delay(speedLevel);
     digitalWrite(ledsPin[i], LOW);
    }
  }
}
// ******************************************
void checkPIR() 
{
  if (digitalRead(pirSensor) == HIGH) {            // check if the input is HIGH
    for (int i=0; i<6; i++)                        // turn ON all LEDs
       digitalWrite(ledsPin[i], HIGH);
    if (pirState == LOW) {                         // we have just turned ON 
      Serial.println("Motion detected!");
      // We only want to print on the output change, not state
      pirState = HIGH;
    }
  } 
  else {
    for (int i=0; i<6; i++)
       digitalWrite(ledsPin[i], LOW);
    if (pirState == HIGH){     // Going down from HIGH to LOW
      // we have just turned of
      Serial.println("Motion ended!");
      // We only want to print on the output change, not state
      pirState = LOW;
    }
  }
}
