# Fritzing sketch led_photo_schematic (saved by Fritzing 0.9.3b)
breadboards: 1

parts:
  Part1 = Arduino Uno (Rev3)
  LED6 = LED - 5mm [color="Red (633nm)" package="5 mm [THT]"]
  R6 = Resistor [tolerance=±5% resistance=220 package=THT]
  R7 = Resistor [tolerance=±5% resistance=10k package=THT]  # not connected
  R8 = Photocell (LDR) [package=THT]

nets:
  N1: Part1.D3_PWM, R8.pin_1
  N2: Part1.GND, R6.Pin_0, R8.pin_0
  N3: LED6.cathode, R6.Pin_1
