# Fritzing sketch led_relay_schematic (saved by Fritzing 0.9.3b)
breadboards: 1

parts:
  Part1 = Arduino Uno (Rev3)
  LED5 = LED - 5mm [color="Yellow (595nm)" package="5 mm [THT]"]
  LED6 = LED - 5mm [color="Red (633nm)" package="5 mm [THT]"]
  R6 = Resistor [tolerance=±5% resistance=220 package=THT]
  R7 = Resistor [tolerance=±5% resistance=10k package=THT]
  S2 = Pushbutton [package="[THT]"]
  Q1 = PNP-Transistor [package="TO92 [THT]"]
  D1 = Rectifier Diode [part_number=1N4001 package="300 mil [THT]"]
  DIP-Relay1 = DIP-Relay-D31A [part_number=D31A*]
  R8 = Resistor [tolerance=±5% resistance=220 package=THT]

nets:
  N1: Part1.D2, R7.Pin_0, S2.Pin_1, S2.Pin_2
  N2: Part1.D3_PWM, R8.Pin_1
  N3: Part1.5V, R6.Pin_0, S2.Pin_3, S2.Pin_4, D1.cathode, DIP-Relay1.A2_Switch_Terminal_A
  N4: Part1.GND, LED5.cathode, LED6.cathode, R7.Pin_1, Q1.C
  N5: LED5.anode, DIP-Relay1.B2_Switch_Terminal_B
  N6: LED6.anode, DIP-Relay1.Coil_Sheeld
  N7: R6.Pin_1, DIP-Relay1.Coil2_-
  N8: Q1.E, D1.anode, DIP-Relay1.A1_Switch_Terminal_A
  N9: Q1.B, R8.Pin_0
