# Fritzing sketch led_rgb_schematic (saved by Fritzing 0.9.3b)
breadboards: 1

parts:
  Part1 = Arduino Uno (Rev3)
  R4 = Resistor [tolerance=±5% resistance=220 package=THT]
  R5 = Resistor [tolerance=±5% resistance=220 package=THT]
  R6 = Resistor [tolerance=±5% resistance=220 package=THT]
  LED1 = RGB LED (com. cathode, rgb) [package="5 mm [THT]"]

nets:
  N1: Part1.D3_PWM, R4.Pin_0
  N2: Part1.D5_PWM, R5.Pin_0
  N3: Part1.D6_PWM, R6.Pin_0
  N4: Part1.GND, LED1.green_anode
  N5: R4.Pin_1, LED1.blue_anode
  N6: R5.Pin_1, LED1.common_cathode
  N7: R6.Pin_1, LED1.red_anode
