# Fritzing sketch motor_throttle_schematic (saved by Fritzing 0.9.3b)
breadboards: 1

parts:
  Part1 = Arduino Uno (Rev3)
  R13 = Rotary Potentiometer (Small) [maximum_resistance=100kΩ package=THT]
  D1 = Rectifier Diode [part_number=1N4001 package="300 mil [THT]"]
  Q1 = PNP-Transistor [package="TO92 [THT]"]
  M1 = DC Motor
  R14 = Resistor [tolerance=±5% resistance=220 package=THT]

nets:
  N1: Part1.A0, R13.wiper
  N2: Part1.D9_PWM, R14.Pin_0
  N3: Part1.5V, R13.leg1, D1.cathode, M1.pin_2
  N4: Part1.GND, R13.leg2, Q1.C
  N5: D1.anode, Q1.E, M1.pin_1
  N6: Q1.B, R14.Pin_1
