# Fritzing sketch servo_test_schematic (saved by Fritzing 0.9.3b)
breadboards: 1

parts:
  Part1 = Arduino Uno (Rev3)
  J1 = Basic Servo
  J2 = Basic Servo
  R11 = Resistor [tolerance=±5% resistance=10k package=THT]
  R12 = Resistor [tolerance=±5% resistance=10k package=THT]
  S3 = Pushbutton [package="[THT]"]
  S4 = Pushbutton [package="[THT]"]

nets:
  N1: Part1.D2, R12.Pin_0, S4.Pin_1, S4.Pin_2
  N2: Part1.D3_PWM, J1.pulse
  N3: Part1.D4, R11.Pin_0, S3.Pin_1, S3.Pin_2
  N4: Part1.D5_PWM, J2.pulse
  VCC: Part1.5V, J1.vcc, J2.vcc, S3.Pin_3, S3.Pin_4, S4.Pin_3, S4.Pin_4
  GND: Part1.GND, J1.gnd, J2.gnd, R11.Pin_1, R12.Pin_1
