# Fritzing sketch shift_register_schematic (saved by Fritzing 0.9.3b)
breadboards: 1

parts:
  Part1 = Arduino Uno (Rev3)
  R1 = Resistor [tolerance=±5% resistance=220 package=THT]
  LED1 = LED - 5mm [color="Red (633nm)" package="5 mm [THT]"]
  LED2 = LED - 5mm [color="Red (633nm)" package="5 mm [THT]"]
  LED3 = LED - 5mm [color="Red (633nm)" package="5 mm [THT]"]
  LED4 = LED - 5mm [color="Red (633nm)" package="5 mm [THT]"]
  LED5 = LED - 5mm [color="Red (633nm)" package="5 mm [THT]"]
  LED6 = LED - 5mm [color="Red (633nm)" package="5 mm [THT]"]
  R2 = Resistor [tolerance=±5% resistance=220 package=THT]
  R3 = Resistor [tolerance=±5% resistance=220 package=THT]
  R4 = Resistor [tolerance=±5% resistance=220 package=THT]
  R5 = Resistor [tolerance=±5% resistance=220 package=THT]
  R6 = Resistor [tolerance=±5% resistance=220 package=THT]
  LED7 = LED - 5mm [color="Red (633nm)" package="5 mm [THT]"]
  LED8 = LED - 5mm [color="Red (633nm)" package="5 mm [THT]"]
  R7 = Resistor [tolerance=±5% resistance=220 package=THT]
  R8 = Resistor [tolerance=±5% resistance=220 package=THT]
  IC1 = IC, DIP package, 16 pins [chip_label=IC]  # not connected

nets:
  N1: Part1.GND, R1.Pin_0, R2.Pin_0, R3.Pin_1, R4.Pin_1, R5.Pin_1, R6.Pin_1, R7.Pin_0, R8.Pin_0
  N2: R1.Pin_1, LED2.cathode
  N3: LED1.cathode, R2.Pin_1
  N4: LED3.cathode, R7.Pin_1
  N5: LED4.cathode, R8.Pin_1
  N6: LED5.cathode, R3.Pin_0
  N7: LED6.cathode, R4.Pin_0
  N8: R5.Pin_0, LED7.cathode
  N9: R6.Pin_0, LED8.cathode
